# Fritzing sketch victoria (saved by Fritzing 0.9.2b)
circuit board: 8.46667cm x 5.64444cm
breadboards: 1

parts:
  Part1 = Arduino Mega 2560 (Rev3)
  Q1 = Basic FET N-Channel [package="TO220 [THT]"]
  R1 = Resistor [tolerance=±5% resistance=100 package=THT]
  R2 = Resistor [tolerance=±5% resistance=10k package=THT]
  GPS = double row male pin header, 6 pins [form="♂ (male)"]
  Power = Header 2 [package=screwterminal-3.5mm-2_lock]
  Q2 = Basic FET N-Channel [package="TO220 [THT]"]
  R3 = Resistor [tolerance=±5% resistance=100 package=THT]
  R4 = Resistor [tolerance=±5% resistance=10k package=THT]
  RF = double row male pin header, 8 pins [form="♂ (male)"]
  GPS1 = male pin header, 4 pins [form="♂ (male)"]
  Q3 = Basic FET N-Channel [package="TO220 [THT]"]
  R5 = Resistor [tolerance=±5% resistance=100 package=THT]
  R6 = Resistor [tolerance=±5% resistance=10k package=THT]

nets:
  N1: Part1.D21/SCL, GPS.pin6, GPS1.pin4
  N2: Part1.D20/SDA, GPS.pin5, GPS1.pin3
  N3: Part1.D15/RX3, GPS.pin2
  N4: Part1.D14/TX3, GPS.pin3
  N5: Part1.GND, Q1.source, R2.Pin_1, Power.2, Q2.source, R4.Pin_1, Q3.source, R6.Pin_1
  N6: Part1.VIN, GPS.pin1, Power.1, RF.pin1, GPS1.pin2
  N7: Part1.D23, R5.Pin_0
  N8: Part1.D24, R1.Pin_0
  N9: Part1.D27, R3.Pin_0
  N10: Part1.D48, RF.pin7
  N11: Part1.D49, RF.pin2
  N12: Part1.D50, RF.pin5
  N13: Part1.D51, RF.pin3
  N14: Part1.D52, RF.pin6
  N15: Q1.gate, R1.Pin_1, R2.Pin_0
  N16: Q1.drain, GPS.pin4
  N17: Q2.gate, R3.Pin_1
  N18: Q2.drain, R4.Pin_0, RF.pin8
  N19: GPS1.pin1, Q3.drain, R6.Pin_0
  N20: Q3.gate, R5.Pin_1
